# Fritzing sketch Consegna-03 (saved by Fritzing 0.9.3b)
breadboards: 2

parts:
  R1 = Resistor [tolerance=±5% resistance=220 package=THT]
  LedON = LED - 5mm [color="Green (555nm)" package="5 mm [THT]"]
  Led_Detected = LED - 5mm [color="Green (555nm)" package="5 mm [THT]"]
  LedTracked = LED - 5mm [color="Red (633nm)" package="5 mm [THT]"]
  R2 = Resistor [tolerance=±5% resistance=220 package=THT]
  R3 = Resistor [tolerance=±5% resistance=220 package=THT]
  Componente1 = Arduino Uno (Rev3)
  Raspberry_Pi_1 = Raspberry Pi 3 [part_number=RPI-3-V1.2]
  ButtonON = Pushbutton [package="[SMD]"]
  ButtonOFF = Pushbutton [package="[SMD]"]
  R4 = Resistor [tolerance=±5% resistance=10k package="2010 [SMD]"]
  R5 = Resistor [tolerance=±5% resistance=10k package="2010 [SMD]"]
  LedConnected = LED - 3mm [color="Green (555nm)" package="3 mm [THT]"]
  R6 = Resistor [tolerance=±5% resistance=220 package="2010 [SMD]"]
  hc-sr1 = hc-sr04
  J1 = Basic Servo
  U1 = POT [package=pot_mammoth]

nets:
  N1: R1.Pin_0, LedON.anode
  N2: R1.Pin_1, Raspberry_Pi_1.GIPO10
  N3: LedON.cathode, Led_Detected.cathode, LedTracked.cathode, Raspberry_Pi_1.GND, R4.Pin_0, R5.Pin_0
  N4: Led_Detected.anode, R2.Pin_0
  N5: LedTracked.anode, R3.Pin_0
  N6: R2.Pin_1, Raspberry_Pi_1.GIPO9
  N7: R3.Pin_1, Raspberry_Pi_1.GIPO7
  N8: Componente1.A2, U1.A
  N9: Componente1.D8, hc-sr1.Trig
  N10: Componente1.D9_PWM, J1.pulse
  N11: Componente1.D4, R6.Pin_1
  N12: Componente1.D7, hc-sr1.Echo
  VCC: Componente1.5V, hc-sr1.VCC, J1.vcc, U1.E
  GND: Componente1.GND, LedConnected.cathode, hc-sr1.GND, J1.gnd, U1.S
  3V3: Raspberry_Pi_1.3v3, Raspberry_Pi_1.5V, ButtonON.Pin_1, ButtonON.Pin_2, ButtonOFF.Pin_1, ButtonOFF.Pin_2
  N13: Raspberry_Pi_1.GPIO3, Raspberry_Pi_1.GIPO4, ButtonOFF.Pin_3, ButtonOFF.Pin_4, R5.Pin_1
  N14: Raspberry_Pi_1.GIPO8, ButtonON.Pin_3, ButtonON.Pin_4, R4.Pin_1
  N15: LedConnected.anode, R6.Pin_0
